// Digital circuit aurora-32.dig as structural Verilog
module aurora_32 (
  input  Clock,
  input  clock_1000hz,
  output [31:0] KSP,
  output [3:0] STATE,
  output [7:0] IR,
  output [31:0] PC,
  output [31:0] KFP,
  output [31:0] USP,
  output [31:0] UFP
);

  wire add_1_c_o, and_1_out, and_2_out, and_5_out, and_6_out, and_7_out, and_8_out, and_9_out, and_10_out,
       and_11_out, and_12_out, and_13_out, and_14_out, and_15_out, and_16_out, and_17_out, and_18_out,
       and_19_out, and_20_out, and_21_out, and_22_out, and_23_out, and_24_out, and_25_out, and_26_out,
       and_27_out, and_28_out, and_29_out, and_30_out, and_31_out, and_32_out, and_33_out, and_34_out,
       and_35_out, and_36_out, and_37_out, and_38_out, and_39_out, and_40_out, and_41_out, and_42_out,
       and_43_out, and_44_out, and_45_out, and_46_out, and_47_out, and_48_out, and_49_out, and_50_out,
       and_51_out, and_52_out, and_53_out, and_54_out, AV_IInstERR, AV_Keyboard, AV_MEMERR, AV_Telnet,
       AV_Tick, bitselector_1_out, clock_t, CLR_IE, CLR_KernelMode, comparator_1_eq, comparator_2_eq,
       comparator_3_eq, comparator_4_eq, comparator_5_eq, comparator_6_eq, comparator_6_lt, comparator_7_eq,
       comparator_7_lt, comparator_8_eq, comparator_9_eq, comparator_10_eq, comparator_11_gt, CS_Bank,
       CS_DMA, CS_DMAlen, CS_DMAorigin, CS_DMAstat, CS_DMAsum, CS_DMAtarget, CS_Gr, CS_Grbgcolor, CS_Grcolor,
       CS_Grdata, CS_Grh, CS_Grmode, CS_Grscale, CS_Grstat, CS_Grw, CS_Grx, CS_Gry, CS_IVT, CS_KeyBoard,
       CS_MIDI, CS_RAM, CS_ROM, CS_Stack, CS_Storage, CS_Telnet, CS_Terminal, CS_Tick, CS_Timer, CS_URAM,
       CS_UROM, CS_UStack, decoder_1_out_0, decoder_1_out_1, delay_1_out, delay_5_out, delay_6_out,
       delay_7_out, delay_8_out, delay_9_out, delay_10_out, DMAstat, DN_SP, driverinvsel_1_out, EN_KSP,
       EN_USP, END_CYCLE, Flag_c, Flag_n, Flag_v, Flag_v_Bus, Flag_z, HALT, INC_PC, INT_REQ, INT_RET,
       INT_TAKE, Kernel_Mode, Kernel_Use_USP, KernelMode_Bus, LD_FP, LD_IR, LD_KFP, LD_KSP, LD_MAR,
       LD_MDREXT, LD_MDRINT, LD_PC, LD_RFlags, LD_Rflags_Bus, LD_Rw, LD_SP, LD_UFP, LD_USP,
       multiplexer_4_out, multiplexer_9_out, multiplexer_11_out, multiplexer_12_out, multiplexer_13_out,
       multiplexer_14_out, multiplexer_15_out, multiplexer_16_out, multiplexer_18_out, nor_2_out, not_1_out,
       not_2_out, not_3_out, not_4_out, not_6_out, not_7_out, not_8_out, not_9_out, not_10_out, not_11_out,
       not_12_out, not_13_out, not_14_out, not_15_out, not_17_out, not_18_out, not_19_out, not_20_out,
       not_21_out, not_22_out, not_23_out, not_24_out, not_25_out, nPSR_q, OE, OE_ALU, OE_FP, OE_INT_REQ,
       OE_KFP, OE_KSP, OE_MDREXT, OE_MDRINT, OE_PC, OE_Ra, OE_Rb, OE_Rflags, OE_SP, OE_UFP, OE_USP, or_1_out,
       or_6_out, or_7_out, or_8_out, or_9_out, or_10_out, or_11_out, or_12_out, or_13_out, or_14_out,
       or_15_out, or_16_out, or_17_out, or_18_out, R_IE_q, SET_IE, SET_KernelMode, Sign_A, Sign_B, Sign_R,
       SignedCalc, sub_1_c_o, Tick_ovf, UP_SP, Use_USP, WE, xnor_2_out, xor_2_out, xor_3_out, xor_4_out,
       xor_5_out, xor_6_out;
  wire [0:0] d_ff_as_1_q, delay_2_out;
  wire [1:0] delay_3_out, multiplexer_27_out;
  wire [2:0] multiplexer_26_out, priorityencoder_1_num;
  wire [3:0] ADDR_Ra, ADDR_Rb, ADDR_Rw, MODE_ALU;
  wire [4:0] div_1_r;
  wire [6:0] RegFile_db;
  wire [7:0] telnet_1_out;
  wire [15:0] keyboard_1_d;
  wire [19:0] div_1_q;
  wire [23:0] Last_Addr, multiplexer_22_out, multiplexer_24_out, multiplexer_25_out;
  wire [30:0] multiplexer_10_out, RegFile_da;
  wire [30:7] RegFile_db_2;
  wire [31:0] add_1_s, add_2_s, add_3_s, add_4_s, add_5_s, add_6_s, add_7_s, add_8_s, and_4_out,
       counter_1_out, Dec_s, Div_S_q, Div_S_r, Div_U_q, Div_U_r, driver_1_out, driver_12_out, Gr_Conx_out,
       Gr_Cony_out, Gr_d, Inc_s, INT_ADDR, Last_Data, MAR_q, MDR_EXT_q, MDR_INT_q, mul_3_mul, mul_5_mul,
       multiplexer_5_out, multiplexer_7_out, multiplexer_8_out, multiplexer_17_out, multiplexer_19_out,
       multiplexer_21_out, multiplexer_28_out, nand_1_out, nor_1_out, not_5_out, or_5_out,
       ramdualaccess_1_d2, register_1_q, register_2_q, register_3_q, register_4_q, register_5_q,
       register_6_q, register_7_q, register_9_q, register_13_q, register_14_q, register_15_q, register_16_q,
       register_17_q, Shift_S_out, Shift_U_out, Storage_d, sub_1_s, Timer_out, xnor_1_out, xor_1_out;
  wire [31:5] div_1_r_2;
  wire [31:20] div_1_q_2, IR_q;
  wire [32:23] multiplexer_3_out;
  wire [34:0] CU_K_d, multiplexer_1_out, multiplexer_2_out;
  wire [35:0] CU_U_d;
  wire [36:0] CU_INT_d;
  wire [63:0] mul_1_mul, mul_2_mul, mul_4_mul, Mul_S_mul, Mul_U_mul, multiplexer_6_out;
  wire [63:32] mul_3_mul_2, mul_5_mul_2;

  assign {driver_1_out[31:5], KernelMode_Bus, Flag_v_Bus, driver_1_out[2:0]} = OE_Rflags ? {{27{1'b0}}, Kernel_Mode, Flag_v, Flag_n, Flag_c, Flag_z} : 32'bz;  // Driver driver_1
  assign {driver_1_out[31:5], KernelMode_Bus, Flag_v_Bus, driver_1_out[2:0]} = OE_INT_REQ ? INT_ADDR : 32'bz;  // Driver driver_2
  CounterPreset #(.maxValue(15), .Bits(4)) u_STATE (
    .en(1'b1), .C(clock_t), .dir(1'b0), .in(4'b0000), .ld(1'b0), .clr(END_CYCLE), .out(STATE));  // open: ovf
  Register #(.Bits(32)) u_IR (
    .D({driver_1_out[31:5], KernelMode_Bus, Flag_v_Bus, driver_1_out[2:0]}), .C(clock_t), .en(LD_IR),
    .Q({IR_q, ADDR_Ra, ADDR_Rb, ADDR_Rw, IR}));
  assign {driver_1_out[31:5], KernelMode_Bus, Flag_v_Bus, driver_1_out[2:0]} = OE_PC ? PC : 32'bz;  // Driver driver_3
  assign {driver_1_out[31:5], KernelMode_Bus, Flag_v_Bus, driver_1_out[2:0]} = OE_Ra ? {Sign_A, RegFile_da} : 32'bz;  // Driver driver_4
  RegisterFile #(.AddrBits(4), .Bits(32)) RegFile (
    .Din({driver_1_out[31:5], KernelMode_Bus, Flag_v_Bus, driver_1_out[2:0]}), .we(LD_Rw), .Rw(ADDR_Rw),
    .C(clock_t), .Ra(ADDR_Ra), .Rb(ADDR_Rb), .Da({Sign_A, RegFile_da}),
    .Db({Sign_B, RegFile_db_2, RegFile_db}));
  assign {driver_1_out[31:5], KernelMode_Bus, Flag_v_Bus, driver_1_out[2:0]} = OE_Rb ? {Sign_B, RegFile_db_2, RegFile_db} : 32'bz;  // Driver driver_5
  CounterPreset #(.Bits(32)) u_KSP (
    .en(EN_KSP), .C(clock_t), .dir(DN_SP),
    .in({driver_1_out[31:5], KernelMode_Bus, Flag_v_Bus, driver_1_out[2:0]}), .ld(LD_KSP), .clr(1'b0),
    .out(KSP));  // open: ovf
  assign {driver_1_out[31:5], KernelMode_Bus, Flag_v_Bus, driver_1_out[2:0]} = OE_KSP ? KSP : 32'bz;  // Driver driver_6
  CounterPreset #(.Bits(32)) u_USP (
    .en(EN_USP), .C(clock_t), .dir(DN_SP),
    .in({driver_1_out[31:5], KernelMode_Bus, Flag_v_Bus, driver_1_out[2:0]}), .ld(LD_USP), .clr(1'b0),
    .out(USP));  // open: ovf
  assign {driver_1_out[31:5], KernelMode_Bus, Flag_v_Bus, driver_1_out[2:0]} = OE_USP ? USP : 32'bz;  // Driver driver_7
  Register #(.Bits(32)) u_KFP (
    .D({driver_1_out[31:5], KernelMode_Bus, Flag_v_Bus, driver_1_out[2:0]}), .C(clock_t), .en(LD_KFP), .Q(KFP));
  assign {driver_1_out[31:5], KernelMode_Bus, Flag_v_Bus, driver_1_out[2:0]} = OE_KFP ? KFP : 32'bz;  // Driver driver_8
  Register #(.Bits(32)) u_UFP (
    .D({driver_1_out[31:5], KernelMode_Bus, Flag_v_Bus, driver_1_out[2:0]}), .C(clock_t), .en(LD_UFP), .Q(UFP));
  assign {driver_1_out[31:5], KernelMode_Bus, Flag_v_Bus, driver_1_out[2:0]} = OE_UFP ? UFP : 32'bz;  // Driver driver_9
  CounterPreset #(.Bits(32), .isProgramCounter("true")) u_PC (
    .en(INC_PC), .C(clock_t), .dir(1'b0),
    .in({driver_1_out[31:5], KernelMode_Bus, Flag_v_Bus, driver_1_out[2:0]}), .ld(LD_PC), .clr(1'b0), .out(PC));  // open: ovf
  JK_FF_AS jk_ff_as_1 (
    .Set(and_1_out), .J(1'b0), .C(clock_t), .K(OE_INT_REQ), .Clr(1'b0), .Q(AV_IInstERR));  // open: nQ
  ROM #(.AddrBits(4), .Bits(37)) CU_INT (.A(STATE), .sel(1'b1), .D(CU_INT_d));
  ROM #(.AddrBits(12), .isProgramMemory("true"), .Bits(36)) CU_U (.A({IR, STATE}), .sel(1'b1), .D(CU_U_d));
  ROM #(.AddrBits(12), .isProgramMemory("true"), .Bits(37)) CU_K (
    .A({IR, STATE}), .sel(1'b1), .D({HALT, Kernel_Use_USP, CU_K_d}));
  or or_1 (or_1_out, UP_SP, DN_SP);
  Comparator #(.Bits(8)) comparator_1 (.a(IR), .b(8'h33), .eq(comparator_1_eq));  // open: gt, lt
  Multiplexer #(.Bits(37)) multiplexer_1 (
    .sel(INT_TAKE), .in_0({37{1'b0}}), .in_1(CU_INT_d), .out({INT_RET, OE_INT_REQ, multiplexer_1_out}));
  not not_1 (not_1_out, Kernel_Mode);
  assign {driver_1_out[31:5], KernelMode_Bus, Flag_v_Bus, driver_1_out[2:0]} = OE_ALU ? {Sign_R, multiplexer_10_out} : 32'bz;  // Driver driver_10
  Demultiplexer demultiplexer_1 (.sel(Use_USP), .in(OE_SP), .out_0(OE_KSP), .out_1(OE_USP));
  Demultiplexer demultiplexer_2 (.sel(Use_USP), .in(LD_SP), .out_0(LD_KSP), .out_1(LD_USP));
  Demultiplexer demultiplexer_3 (.sel(Use_USP), .in(or_1_out), .out_0(EN_KSP), .out_1(EN_USP));
  Demultiplexer demultiplexer_4 (.sel(Use_USP), .in(OE_FP), .out_0(OE_KFP), .out_1(OE_UFP));
  Demultiplexer demultiplexer_5 (.sel(Use_USP), .in(LD_FP), .out_0(LD_KFP), .out_1(LD_UFP));
  and and_1 (and_1_out, not_1_out, CU_U_d[35]);
  Multiplexer #(.Bits(35)) multiplexer_2 (
    .sel(Kernel_Mode), .in_0(CU_U_d[34:0]), .in_1(CU_K_d), .out(multiplexer_2_out));
  assign driverinvsel_1_out = ~comparator_1_eq ? and_6_out : 1'bz;  // DriverInvSel driverinvsel_1
  or or_2 (INC_PC, multiplexer_3_out[23], driverinvsel_1_out);
  Multiplexer #(.Bits(35)) multiplexer_3 (
    .sel(INT_TAKE), .in_0(multiplexer_2_out), .in_1(multiplexer_1_out),
    .out({SET_KernelMode, CLR_KernelMode, multiplexer_3_out[32:31], SignedCalc, MODE_ALU, WE, OE, multiplexer_3_out[23], SET_IE, CLR_IE, OE_ALU, OE_Rflags, OE_Rb, OE_Ra, OE_MDREXT, OE_MDRINT, OE_PC, OE_SP, OE_FP, LD_Rflags_Bus, LD_RFlags, LD_Rw, LD_IR, LD_MDREXT, LD_MDRINT, LD_MAR, LD_PC, LD_SP, LD_FP, UP_SP, DN_SP}));
  not not_2 (not_2_out, HALT);
  or or_3 (Use_USP, Kernel_Use_USP, not_3_out);
  not not_3 (not_3_out, Kernel_Mode);
  or or_4 (END_CYCLE, and_6_out, multiplexer_3_out[32]);
  not not_4 (not_4_out, Flag_z);
  and and_2 (and_2_out, not_4_out, not_13_out);
  and and_3 (clock_t, Clock, not_2_out);
  Add #(.Bits(32)) add_1 (
    .a({Sign_A, RegFile_da}), .b({Sign_B, RegFile_db_2, RegFile_db}), .c_i(1'b0), .s(add_1_s), .c_o(add_1_c_o));
  Sub #(.Bits(32)) sub_1 (
    .a({Sign_A, RegFile_da}), .b({Sign_B, RegFile_db_2, RegFile_db}), .c_i(1'b0), .s(sub_1_s), .c_o(sub_1_c_o));
  BarrelShifter #(.Bits(32), .barrelSigned("true")) Shift_U (
    .in({Sign_A, RegFile_da}), .shift(RegFile_db), .out(Shift_U_out));
  assign and_4_out = {Sign_A, RegFile_da} & {Sign_B, RegFile_db_2, RegFile_db};  // And and_4, 32 bits wide
  assign nand_1_out = ~({Sign_A, RegFile_da} & {Sign_B, RegFile_db_2, RegFile_db});  // NAnd nand_1, 32 bits wide
  assign or_5_out = {Sign_A, RegFile_da} | {Sign_B, RegFile_db_2, RegFile_db};  // Or or_5, 32 bits wide
  assign nor_1_out = ~({Sign_A, RegFile_da} | {Sign_B, RegFile_db_2, RegFile_db});  // NOr nor_1, 32 bits wide
  assign xor_1_out = {Sign_A, RegFile_da} ^ {Sign_B, RegFile_db_2, RegFile_db};  // XOr xor_1, 32 bits wide
  assign xnor_1_out = ~({Sign_A, RegFile_da} ^ {Sign_B, RegFile_db_2, RegFile_db});  // XNOr xnor_1, 32 bits wide
  assign not_5_out = ~{Sign_A, RegFile_da};  // Not not_5, 32 bits wide
  Add #(.Bits(32)) Inc (.a({Sign_A, RegFile_da}), .b(32'h1), .c_i(1'b0), .s(Inc_s));  // open: c_o
  Sub #(.Bits(32)) Dec (.a({Sign_A, RegFile_da}), .b(32'h1), .c_i(1'b0), .s(Dec_s));  // open: c_o
  not not_6 (not_6_out, Flag_c);
  and and_5 (and_5_out, not_6_out, not_7_out);
  not not_7 (not_7_out, Flag_z);
  not not_8 (not_8_out, Flag_c);
  not not_9 (not_9_out, Flag_z);
  not not_10 (not_10_out, and_5_out);
  xor xor_2 (xor_2_out, Flag_n, Flag_v);
  not not_11 (not_11_out, xor_2_out);
  not not_12 (not_12_out, and_2_out);
  not not_13 (not_13_out, xor_2_out);
  BarrelShifter #(.Bits(32), .barrelShifterMode("arithmetic"), .barrelSigned("true")) Shift_S (
    .in({Sign_A, RegFile_da}), .shift(RegFile_db), .out(Shift_S_out));
  Multiplexer #(.Selector_Bits(4)) multiplexer_4 (
    .sel(IR_q[23:20]), .in_0(1'b0), .in_1(Flag_c), .in_2(Flag_z), .in_3(and_5_out), .in_4(not_8_out),
    .in_5(not_9_out), .in_6(not_10_out), .in_7(Flag_n), .in_8(Flag_v), .in_9(xor_2_out), .in_10(not_11_out),
    .in_11(and_2_out), .in_12(not_12_out), .in_13(1'b0), .in_14(1'b0), .in_15(1'b0), .out(multiplexer_4_out));
  not not_14 (not_14_out, multiplexer_4_out);
  Mul #(.Bits(32)) Mul_U (.a({Sign_A, RegFile_da}), .b({Sign_B, RegFile_db_2, RegFile_db}), .mul(Mul_U_mul));
  Mul #(.Signed("true"), .Bits(32)) Mul_S (
    .a({Sign_A, RegFile_da}), .b({Sign_B, RegFile_db_2, RegFile_db}), .mul(Mul_S_mul));
  Div #(.Bits(32)) Div_U (.a({Sign_A, RegFile_da}), .b({Sign_B, RegFile_db_2, RegFile_db}), .q(Div_U_q), .r(Div_U_r));
  Div #(.remainderPositive("false"), .Signed("true"), .Bits(32)) Div_S (
    .a({Sign_A, RegFile_da}), .b({Sign_B, RegFile_db_2, RegFile_db}), .q(Div_S_q), .r(Div_S_r));
  Multiplexer #(.Bits(32)) multiplexer_5 (
    .sel(SignedCalc), .in_0(Shift_U_out), .in_1(Shift_S_out), .out(multiplexer_5_out));
  and and_6 (and_6_out, multiplexer_3_out[31], not_14_out);
  Multiplexer #(.Bits(64)) multiplexer_6 (
    .sel(SignedCalc), .in_0(Mul_U_mul), .in_1(Mul_S_mul), .out(multiplexer_6_out));
  Multiplexer #(.Bits(32)) multiplexer_7 (.sel(SignedCalc), .in_0(Div_U_q), .in_1(Div_S_q), .out(multiplexer_7_out));
  Multiplexer #(.Bits(32)) multiplexer_8 (.sel(SignedCalc), .in_0(Div_U_r), .in_1(Div_S_r), .out(multiplexer_8_out));
  RS_FF R_IE (.S(SET_IE), .C(clock_t), .R(CLR_IE), .Q(R_IE_q));  // open: nQ
  xor xor_3 (xor_3_out, SET_KernelMode, CLR_KernelMode);
  and and_7 (and_7_out, END_CYCLE, INT_REQ, R_IE_q);
  not not_15 (not_15_out, KernelMode_Bus);
  or or_6 (or_6_out, xor_3_out, LD_Rflags_Bus);
  Register #(.Bits(32)) MAR (
    .D({driver_1_out[31:5], KernelMode_Bus, Flag_v_Bus, driver_1_out[2:0]}), .C(clock_t), .en(LD_MAR),
    .Q(MAR_q));
  assign {driver_1_out[31:5], KernelMode_Bus, Flag_v_Bus, driver_1_out[2:0]} = OE_MDRINT ? MDR_INT_q : 32'bz;  // Driver driver_11
  RS_FF rs_ff_1 (.S(and_7_out), .C(clock_t), .R(INT_RET), .Q(INT_TAKE));  // open: nQ
  Multiplexer multiplexer_9 (.sel(LD_Rflags_Bus), .in_0(CLR_KernelMode), .in_1(not_15_out), .out(multiplexer_9_out));
  Register nPSR (.D(multiplexer_9_out), .C(clock_t), .en(or_6_out), .Q(nPSR_q));
  Decoder decoder_1 (.sel(MAR_q[31]), .out_0(decoder_1_out_0), .out_1(decoder_1_out_1));
  Register #(.Bits(32)) MDR_EXT (
    .D({driver_1_out[31:5], KernelMode_Bus, Flag_v_Bus, driver_1_out[2:0]}), .C(clock_t), .en(LD_MDREXT),
    .Q(MDR_EXT_q));
  not not_16 (Kernel_Mode, nPSR_q);
  Multiplexer #(.Selector_Bits(4), .Bits(32)) multiplexer_10 (
    .sel(MODE_ALU), .in_0(add_1_s), .in_1(sub_1_s), .in_2(multiplexer_6_out[31:0]), .in_3(multiplexer_7_out),
    .in_4(multiplexer_5_out), .in_5(and_4_out), .in_6(nand_1_out), .in_7(or_5_out), .in_8(nor_1_out),
    .in_9(xor_1_out), .in_10(xnor_1_out), .in_11(not_5_out), .in_12(Inc_s), .in_13(Dec_s),
    .in_14(multiplexer_8_out), .in_15({32{1'b0}}), .out({Sign_R, multiplexer_10_out}));
  xnor xnor_2 (xnor_2_out, Sign_A, Sign_B);
  xor xor_4 (xor_4_out, Sign_A, Sign_B);
  Delay delay_1 (.in(driver_1_out[31]), .out(delay_1_out));
  not not_17 (not_17_out, Kernel_Mode);
  and and_8 (and_8_out, decoder_1_out_0, Kernel_Mode);
  Register #(.Bits(32)) MDR_INT (.D(driver_12_out), .C(clock_t), .en(LD_MDRINT), .Q(MDR_INT_q));
  assign driver_12_out = OE_MDREXT ? MDR_EXT_q : 32'bz;  // Driver driver_12
  xor xor_5 (xor_5_out, Sign_A, Sign_R);
  xor xor_6 (xor_6_out, Sign_A, Sign_R);
  and and_9 (and_9_out, delay_1_out, not_17_out);
  Demultiplexer #(.Selector_Bits(4)) demultiplexer_6 (
    .sel(MAR_q[27:24]), .in(and_8_out), .out_0(CS_ROM), .out_1(CS_RAM), .out_2(CS_Stack), .out_3(CS_IVT),
    .out_4(CS_KeyBoard), .out_5(CS_Terminal), .out_6(CS_Telnet), .out_7(CS_Tick), .out_8(CS_Timer),
    .out_9(CS_Gr), .out_10(CS_MIDI), .out_11(CS_Storage), .out_12(CS_DMA), .out_13(CS_Bank));  // open: out_14, out_15
  Comparator #(.Bits(4)) comparator_2 (.a(MODE_ALU), .b(4'b0001), .eq(comparator_2_eq));  // open: gt, lt
  and and_10 (and_10_out, xnor_2_out, xor_5_out);
  and and_11 (and_11_out, xor_4_out, xor_6_out);
  and and_12 (and_12_out, WE, CS_Grx);
  and and_13 (and_13_out, WE, CS_Gry);
  and and_14 (and_14_out, WE, CS_Grcolor);
  and and_15 (and_15_out, WE, CS_Grw);
  and and_16 (and_16_out, WE, CS_Grh);
  assign driver_12_out = and_18_out ? {{31{1'b0}}, d_ff_as_1_q[0]} : 32'bz;  // Driver driver_13
  and and_17 (and_17_out, clock_t, WE, CS_Grstat);
  and and_18 (and_18_out, OE, CS_Grstat);
  and and_19 (and_19_out, WE, CS_Grdata);
  and and_20 (and_20_out, WE, CS_Grbgcolor);
  and and_21 (and_21_out, WE, CS_Grmode);
  Comparator #(.Bits(32)) comparator_3 (
    .a({32{1'b0}}), .b({Sign_R, multiplexer_10_out}), .eq(comparator_3_eq));  // open: gt, lt
  Multiplexer multiplexer_11 (
    .sel(not_21_out), .in_0(driver_1_out[1]), .in_1(multiplexer_12_out), .out(multiplexer_11_out));
  Multiplexer multiplexer_12 (.sel(comparator_2_eq), .in_0(add_1_c_o), .in_1(sub_1_c_o), .out(multiplexer_12_out));
  Multiplexer multiplexer_13 (.sel(comparator_2_eq), .in_0(and_10_out), .in_1(and_11_out), .out(multiplexer_13_out));
  and and_22 (and_22_out, LD_MAR, nor_2_out, and_9_out);
  Comparator #(.Bits(7)) comparator_4 (.a(MAR_q[30:24]), .b({7{1'b0}}), .eq(comparator_4_eq));  // open: gt, lt
  not not_18 (not_18_out, comparator_4_eq);
  Comparator #(.Bits(7)) comparator_5 (.a(MAR_q[30:24]), .b(7'b0000011), .eq(comparator_5_eq));  // open: gt, lt
  not not_19 (not_19_out, comparator_5_eq);
  Demultiplexer #(.Selector_Bits(3)) demultiplexer_7 (
    .sel(MAR_q[26:24]), .in(decoder_1_out_1), .out_0(CS_UROM), .out_1(CS_URAM), .out_2(CS_UStack));  // open: out_3, out_4, out_5, out_6, out_7
  Register #(.Bits(32)) register_1 (.D(driver_12_out), .C(clock_t), .en(and_12_out), .Q(register_1_q));
  Register #(.Bits(32)) register_2 (.D(driver_12_out), .C(clock_t), .en(and_13_out), .Q(register_2_q));
  Register #(.Bits(32)) register_3 (.D(driver_12_out), .C(clock_t), .en(and_14_out), .Q(register_3_q));
  Register #(.Bits(32)) register_4 (.D(driver_12_out), .C(clock_t), .en(and_15_out), .Q(register_4_q));
  Register #(.Bits(32)) register_5 (.D(driver_12_out), .C(clock_t), .en(and_16_out), .Q(register_5_q));
  D_FF_AS d_ff_as_1 (
    .Set(1'b0), .D(driver_12_out[0]), .C(and_17_out), .Clr(comparator_7_eq), .Q(d_ff_as_1_q[0]));  // open: nQ
  RAMDualAccess #(.AddrBits(20), .Bits(32)) ramdualaccess_1 (
    .str(and_19_out), .C(clock_t), .ld(1'b1), .A1(multiplexer_22_out[19:0]), .Din1(driver_12_out),
    .A2(div_1_q), .D2(ramdualaccess_1_d2));  // open: D1
  Register #(.Bits(32)) register_6 (.D(driver_12_out), .C(clock_t), .en(and_20_out), .Q(register_6_q));
  Register #(.Bits(32)) register_7 (.D(driver_12_out), .C(clock_t), .en(and_21_out), .Q(register_7_q));
  not not_20 (not_20_out, LD_Rflags_Bus);
  Multiplexer multiplexer_14 (
    .sel(not_20_out), .in_0(driver_1_out[0]), .in_1(comparator_3_eq), .out(multiplexer_14_out));
  not not_21 (not_21_out, LD_Rflags_Bus);
  Multiplexer multiplexer_15 (.sel(not_22_out), .in_0(driver_1_out[2]), .in_1(Sign_R), .out(multiplexer_15_out));
  not not_22 (not_22_out, LD_Rflags_Bus);
  Multiplexer multiplexer_16 (.sel(not_23_out), .in_0(Flag_v_Bus), .in_1(multiplexer_13_out), .out(multiplexer_16_out));
  or or_7 (or_7_out, LD_Rflags_Bus, LD_RFlags);
  not not_23 (not_23_out, LD_Rflags_Bus);
  nor nor_2 (nor_2_out, not_18_out, not_19_out);
  Comparator #(.Bits(32)) comparator_6 (
    .a(Gr_Conx_out), .b(register_4_q), .eq(comparator_6_eq), .lt(comparator_6_lt));  // open: gt
  and and_23 (and_23_out, d_ff_as_1_q[0], comparator_6_lt);
  Comparator #(.Bits(32)) comparator_7 (
    .a(Gr_Cony_out), .b(register_5_q), .eq(comparator_7_eq), .lt(comparator_7_lt));  // open: gt
  and and_24 (and_24_out, WE, CS_Grscale);
  or or_8 (or_8_out, LD_Rflags_Bus, LD_RFlags);
  or or_9 (or_9_out, LD_Rflags_Bus, LD_RFlags);
  or or_10 (or_10_out, LD_Rflags_Bus, LD_RFlags);
  Register register_8 (.D(multiplexer_16_out), .C(clock_t), .en(or_7_out), .Q(Flag_v));
  JK_FF_AS jk_ff_as_2 (.Set(and_22_out), .J(1'b0), .C(clock_t), .K(OE_INT_REQ), .Clr(1'b0), .Q(AV_MEMERR));  // open: nQ
  Demultiplexer #(.Selector_Bits(3)) demultiplexer_8 (
    .sel(MAR_q[2:0]), .in(CS_DMA), .out_0(CS_DMAorigin), .out_1(CS_DMAtarget), .out_2(CS_DMAlen),
    .out_3(CS_DMAstat), .out_4(CS_DMAsum));  // open: out_5, out_6, out_7
  CounterPreset #(.Bits(32)) Gr_Conx (
    .en(and_23_out), .C(clock_t), .dir(1'b0), .in({32{1'b0}}), .ld(1'b0), .clr(comparator_6_eq),
    .out(Gr_Conx_out));  // open: ovf
  CounterPreset #(.Bits(32)) Gr_Cony (
    .en(comparator_6_eq), .C(clock_t), .dir(1'b0), .in({32{1'b0}}), .ld(1'b0), .clr(comparator_7_eq),
    .out(Gr_Cony_out));  // open: ovf
  BitSelector #(.Selector_Bits(5)) bitselector_1 (.in(ramdualaccess_1_d2), .sel(div_1_r), .out(bitselector_1_out));
  Register #(.Bits(32)) register_9 (.D(driver_12_out), .C(clock_t), .en(and_24_out), .Q(register_9_q));
  Register register_10 (.D(multiplexer_14_out), .C(clock_t), .en(or_8_out), .Q(Flag_z));
  Register register_11 (.D(multiplexer_11_out), .C(clock_t), .en(or_9_out), .Q(Flag_c));
  Register register_12 (.D(multiplexer_15_out), .C(clock_t), .en(or_10_out), .Q(Flag_n));
  Demultiplexer #(.Selector_Bits(4)) demultiplexer_9 (
    .sel(MAR_q[23:20]), .in(CS_Gr), .out_0(CS_Grx), .out_1(CS_Gry), .out_2(CS_Grw), .out_3(CS_Grh),
    .out_4(CS_Grcolor), .out_5(CS_Grbgcolor), .out_6(CS_Grdata), .out_7(CS_Grscale), .out_8(CS_Grmode),
    .out_9(CS_Grstat));  // open: out_10, out_11, out_12, out_13, out_14, out_15
  Mul #(.Bits(32)) mul_1 (.a(register_4_q), .b(Gr_Cony_out), .mul(mul_1_mul));
  Multiplexer #(.Bits(32)) multiplexer_17 (
    .sel(bitselector_1_out), .in_0(register_6_q), .in_1(register_3_q), .out(multiplexer_17_out));
  Add #(.Bits(32)) add_2 (.a(register_1_q), .b(Gr_Conx_out), .c_i(1'b0), .s(add_2_s));  // open: c_o
  Add #(.Bits(32)) add_3 (.a(Gr_Cony_out), .b(register_2_q), .c_i(1'b0), .s(add_3_s));  // open: c_o
  Mul #(.Bits(32)) mul_2 (.a(mul_1_mul[31:0]), .b(mul_3_mul), .mul(mul_2_mul));
  Mul #(.Bits(32)) mul_3 (.a(multiplexer_19_out), .b(multiplexer_19_out), .mul({mul_3_mul_2, mul_3_mul}));
  Comparator #(.Bits(32)) comparator_8 (.a(32'h1), .b(register_7_q), .eq(comparator_8_eq));  // open: gt, lt
  Comparator #(.Bits(32)) comparator_9 (.a(32'h2), .b(register_7_q), .eq(comparator_9_eq));  // open: gt, lt
  Mul #(.Bits(32)) mul_4 (.a(32'h1e0), .b(add_3_s), .mul(mul_4_mul));
  Add #(.Bits(32)) add_4 (.a(mul_5_mul), .b(mul_2_mul[31:0]), .c_i(1'b0), .s(add_4_s));  // open: c_o
  Div #(.Bits(32)) div_1 (.a(add_4_s), .b(32'h20), .q({div_1_q_2, div_1_q}), .r({div_1_r_2, div_1_r}));
  Comparator #(.Bits(32)) comparator_10 (.a(register_9_q), .b({32{1'b0}}), .eq(comparator_10_eq));  // open: gt, lt
  and and_25 (and_25_out, WE, CS_DMAorigin);
  and and_26 (and_26_out, WE, CS_DMAtarget);
  and and_27 (and_27_out, WE, CS_DMAlen);
  and and_28 (and_28_out, clock_t, WE, CS_DMAstat);
  and and_29 (and_29_out, OE, CS_DMAstat);
  and and_30 (and_30_out, WE, CS_Bank);
  and and_31 (and_31_out, OE, CS_Bank);
  Add #(.Bits(32)) add_5 (.a(add_2_s), .b(mul_4_mul[31:0]), .c_i(1'b0), .s(add_5_s));  // open: c_o
  Mul #(.Bits(32)) mul_5 (.a(Gr_Conx_out), .b(multiplexer_19_out), .mul({mul_5_mul_2, mul_5_mul}));
  and and_32 (and_32_out, and_23_out, comparator_7_lt);
  Register #(.Bits(32)) register_13 (.D(driver_12_out), .C(clock_t), .en(and_25_out), .Q(register_13_q));
  Register #(.Bits(32)) register_14 (.D(driver_12_out), .C(clock_t), .en(and_26_out), .Q(register_14_q));
  Register #(.Bits(32)) register_15 (.D(driver_12_out), .C(clock_t), .en(and_27_out), .Q(register_15_q));
  assign driver_12_out = and_29_out ? {{31{1'b0}}, DMAstat} : 32'bz;  // Driver driver_14
  D_FF_AS d_ff_as_2 (
    .Set(1'b0), .D(driver_12_out[0]), .C(and_28_out), .Clr(comparator_11_gt), .Q(DMAstat));  // open: nQ
  and and_33 (and_33_out, WE, CS_DMAsum);
  Register #(.Bits(32)) register_16 (.D(driver_12_out), .C(clock_t), .en(and_30_out), .Q(register_16_q));
  assign driver_12_out = and_31_out ? register_16_q : 32'bz;  // Driver driver_15
  Multiplexer multiplexer_18 (.sel(comparator_9_eq), .in_0(and_32_out), .in_1(and_34_out), .out(multiplexer_18_out));
  and and_34 (and_34_out, and_32_out, bitselector_1_out);
  Multiplexer #(.Bits(32)) multiplexer_19 (
    .sel(comparator_10_eq), .in_0(register_9_q), .in_1(32'h1), .out(multiplexer_19_out));
  PriorityEncoder #(.Selector_Bits(3)) priorityencoder_1 (
    .in0(1'b0), .in1(AV_Telnet), .in2(AV_Keyboard), .in3(1'b0), .in4(AV_Tick), .in5(1'b0), .in6(AV_MEMERR),
    .in7(AV_IInstERR), .num(priorityencoder_1_num), .any(INT_REQ));
  GraphicCard #(.graphicHeight(240), .graphicWidth(480), .Bits(32)) Gr (
    .A(add_5_s[17:0]), .str(multiplexer_18_out), .C(clock_t), .ld(1'b0), .B(1'b0), .D(Gr_d));
  Multiplexer #(.Selector_Bits(3), .Bits(32)) multiplexer_20 (
    .sel(priorityencoder_1_num), .in_0(32'h3000003), .in_1(32'h3000002), .in_2(32'h3000001),
    .in_3(32'h3000000), .in_4(32'h3000007), .in_5(32'h3000006), .in_6(32'h3000004), .in_7(32'h3000005),
    .out(INT_ADDR));
  Counter #(.Bits(32)) counter_1 (.en(DMAstat), .C(clock_t), .clr(comparator_11_gt), .out(counter_1_out));  // open: ovf
  Multiplexer #(.Bits(32)) multiplexer_21 (
    .sel(DMAstat), .in_0(driver_12_out), .in_1(add_8_s), .out(multiplexer_21_out));
  or or_11 (or_11_out, and_33_out, DMAstat);
  Multiplexer #(.Bits(24)) multiplexer_22 (
    .sel(Kernel_Mode), .in_0({register_16_q[1:0], MAR_q[21:0]}), .in_1(MAR_q[23:0]), .out(multiplexer_22_out));
  Multiplexer #(.Bits(32)) multiplexer_23 (
    .sel(comparator_8_eq), .in_0(register_3_q), .in_1(multiplexer_17_out), .out(Gr_d));
  Add #(.Bits(32)) add_6 (.a(register_13_q), .b(counter_1_out), .c_i(1'b0), .s(add_6_s));  // open: c_o
  Add #(.Bits(32)) add_7 (.a(register_14_q), .b(counter_1_out), .c_i(1'b0), .s(add_7_s));  // open: c_o
  Comparator #(.Bits(32)) comparator_11 (.a(counter_1_out), .b(register_15_q), .gt(comparator_11_gt));  // open: eq, lt
  Register #(.Bits(32)) register_17 (.D(multiplexer_21_out), .C(clock_t), .en(or_11_out), .Q(register_17_q));
  Multiplexer #(.Bits(24)) multiplexer_24 (
    .sel(DMAstat), .in_0(multiplexer_22_out), .in_1(add_6_s[23:0]), .out(multiplexer_24_out));
  Multiplexer #(.Bits(24)) multiplexer_25 (
    .sel(DMAstat), .in_0(multiplexer_22_out), .in_1(add_7_s[23:0]), .out(multiplexer_25_out));
  Sub #(.Bits(24)) sub_2 (.a(add_7_s[23:0]), .b(24'h1), .c_i(1'b0), .s(Last_Addr));  // open: c_o
  Add #(.Bits(32)) add_8 (.a(Last_Data), .b(register_17_q), .c_i(1'b0), .s(add_8_s));  // open: c_o
  assign driver_12_out = and_35_out ? register_17_q : 32'bz;  // Driver driver_16
  and and_35 (and_35_out, CS_DMAsum, OE);
  or or_12 (or_12_out, WE, OE);
  and and_36 (and_36_out, CS_KeyBoard, OE);
  and and_37 (and_37_out, CS_Terminal, WE);
  and and_38 (and_38_out, CS_Telnet, WE);
  and and_39 (and_39_out, CS_Telnet, OE);
  and and_40 (and_40_out, WE, CS_MIDI);
  Delay delay_2 (.in(and_46_out), .out(delay_2_out[0]));
  Multiplexer #(.Bits(3)) multiplexer_26 (
    .sel(DMAstat), .in_0({OE, WE, delay_2_out[0]}), .in_1(3'b101), .out(multiplexer_26_out));
  or or_13 (or_13_out, WE, OE);
  Delay delay_3 (.in(and_47_out), .out(delay_3_out[0]));
  Multiplexer #(.Bits(2)) multiplexer_27 (.sel(DMAstat), .in_0(delay_3_out), .in_1(2'b01), .out(multiplexer_27_out));
  Delay delay_4 (.in(and_41_out), .out(delay_3_out[1]));
  and and_41 (and_41_out, CS_UROM, OE);
  EEPROM #(.AddrBits(24), .Bits(32)) ROM (
    .A(multiplexer_22_out), .CS(delay_5_out), .WE(WE), .OE(OE), .D(driver_12_out));
  Delay delay_5 (.in(and_50_out), .out(delay_5_out));
  or or_14 (or_14_out, WE, OE);
  RAMSinglePortSel #(.AddrBits(24), .Bits(32)) RAM (
    .A(multiplexer_22_out), .CS(delay_6_out), .WE(WE), .OE(OE), .D(driver_12_out));
  Delay delay_6 (.in(and_42_out), .out(delay_6_out));
  and and_42 (and_42_out, CS_RAM, or_15_out);
  or or_15 (or_15_out, WE, OE);
  RAMSinglePortSel #(.AddrBits(24), .Bits(32)) Stack (
    .A(multiplexer_22_out), .CS(delay_7_out), .WE(WE), .OE(OE), .D(driver_12_out));
  Delay delay_7 (.in(and_43_out), .out(delay_7_out));
  and and_43 (and_43_out, CS_Stack, or_16_out);
  or or_16 (or_16_out, WE, OE);
  RAMSinglePortSel #(.AddrBits(24), .Bits(32)) IVT (
    .A(multiplexer_22_out), .CS(delay_8_out), .WE(WE), .OE(OE), .D(driver_12_out));
  Delay delay_8 (.in(and_44_out), .out(delay_8_out));
  and and_44 (and_44_out, CS_IVT, or_12_out);
  Keyboard keyboard_1 (.C(clock_t), .en(and_36_out), .D(keyboard_1_d), .av(AV_Keyboard));
  Terminal terminal_1 (.D(driver_12_out[15:0]), .C(clock_t), .en(and_37_out));
  Telnet #(.port(8081)) telnet_1 (
    .in(driver_12_out[7:0]), .C(clock_t), .wr(and_38_out), .rd(and_39_out), .out(telnet_1_out), .av(AV_Telnet));
  and and_45 (and_45_out, CS_Tick, OE);
  Counter #(.Bits(14)) Tick (.en(1'b1), .C(clock_t), .clr(CS_Tick), .ovf(Tick_ovf));  // open: out
  Counter #(.Bits(32)) Timer (.en(not_24_out), .C(clock_1000hz), .clr(1'b0), .out(Timer_out));  // open: ovf
  not not_24 (not_24_out, HALT);
  // MIDI #(.midiProgChange("true"), .midiChannel(16)) MIDI: pin names not known; wires that end beside it: driver_12_out[6:0], driver_12_out[7], driver_12_out[8], and_40_out, clock_t
  EEPROM #(.AddrBits(24), .Bits(32)) Storage (
    .A(multiplexer_24_out), .CS(multiplexer_26_out[0]), .WE(multiplexer_26_out[1]),
    .OE(multiplexer_26_out[2]), .D(Storage_d));
  and and_46 (and_46_out, CS_Storage, or_13_out);
  and and_47 (and_47_out, CS_UROM, WE);
  RAMSinglePortSel #(.AddrBits(24), .Bits(32)) URAM (
    .A(multiplexer_22_out), .CS(delay_9_out), .WE(WE), .OE(OE), .D(driver_12_out));
  Delay delay_9 (.in(and_48_out), .out(delay_9_out));
  and and_48 (and_48_out, CS_URAM, or_17_out);
  or or_17 (or_17_out, WE, OE);
  RAMSinglePortSel #(.AddrBits(24), .Bits(32)) UStack (
    .A(multiplexer_22_out), .CS(delay_10_out), .WE(WE), .OE(OE), .D(driver_12_out));
  Delay delay_10 (.in(and_49_out), .out(delay_10_out));
  and and_49 (and_49_out, CS_UStack, or_18_out);
  or or_18 (or_18_out, WE, OE);
  and and_50 (and_50_out, CS_ROM, or_14_out);
  assign driver_12_out = and_53_out ? {{16{1'b0}}, keyboard_1_d} : 32'bz;  // Driver driver_17
  RS_FF_AS rs_ff_as_1 (.S(Tick_ovf), .R(CS_Tick), .Q(AV_Tick));  // open: nQ
  and and_51 (and_51_out, CS_Storage, WE);
  and and_52 (and_52_out, multiplexer_26_out[0], multiplexer_26_out[2], not_25_out);
  not not_25 (not_25_out, DMAstat);
  RAMDualAccess #(.AddrBits(24), .Bits(32)) UROM (
    .str(multiplexer_27_out[0]), .C(clock_t), .ld(multiplexer_27_out[1]), .A1(multiplexer_25_out),
    .Din1(multiplexer_28_out), .A2(Last_Addr), .D1(driver_12_out), .D2(Last_Data));
  and and_53 (and_53_out, CS_KeyBoard, OE);
  and and_54 (and_54_out, CS_Telnet, OE);
  assign driver_12_out = and_54_out ? {{24{1'b0}}, telnet_1_out} : 32'bz;  // Driver driver_18
  assign driver_12_out = and_45_out ? 32'h1 : 32'bz;  // Driver driver_19
  assign driver_12_out = CS_Timer ? Timer_out : 32'bz;  // Driver driver_20
  assign Storage_d = and_51_out ? driver_12_out : 32'bz;  // Driver driver_21
  assign driver_12_out = and_52_out ? Storage_d : 32'bz;  // Driver driver_22
  Multiplexer #(.Bits(32)) multiplexer_28 (
    .sel(DMAstat), .in_0(driver_12_out), .in_1(Storage_d), .out(multiplexer_28_out));

  // Notes on the sheet:
  //   Clock: Hz: 6553600
  //   clock_1000hz: Hz: 1000
  //   CU
  //   contents of CU_INT (hex, n*v repeats v):
  //   3c280080,43c000000,3c002020,3e010002,3c002020,3c004080,3e010002
  //   ,83c000020,3d000040,113c008010
  //   contents of CU_U (hex, n*v repeats v):
  //   3c004020,3d800040,3c008100,13c000000,12*3c000000,3c004020,3d800040
  //   ,3c008100,13c000000,12*3c000000,3c004020,3d800040,3c008100,13c000000
  //   ,12*3c000000,3c004020,3d800040,3c008100,13c000000,12*3c000000
  //   ,3c004020,3d800040,3c008100,13c000000,12*3c000000,3c004020,3d800040
  //   ,3c008100,13c000000,12*3c000000,3c004020,3d800040,3c008100,13c000000
  //   ,12*3c000000,3c004020,3d800040,3c008100,13c000000,12*3c000000
  //   ,3c004020,3d800040,3c008100,13c000000,12*3c000000,3c004020,3d800040
  //   ,3c008100,13c000000,12*3c000000,3c004020,3d800040,3c008100,13c000000
  //   ,12*3c000000,3c004020,3d800040,3c008100,13c000000,12*3c000000
  //   ,3c004020,3d800040,3c008100,13c000000,12*3c000000,3c004020,3d800040
  //   ,3c008100,13c000000,12*3c000000,3c004020,3d800040,3c008100,13c000000
  //   ,12*3c000000,3c004020,3d800040,3c008100,13c000000,12*3c000000
  //   ,3c004020,3d800040,3c008100,13c020200,12*3c000000,3c004020,3d800040
  //   ,3c008100,3c040020,3d000040,13c008200,10*3c000000,3c004020,3d800040
  //   ,3c008100,3c040020,3c020080,13e010000,10*3c000000,3c004020,3d800040
  //   ,3c008100,3c004020,3d800040,3c008020,3d000040,13c008200,8*3c000000
  //   ,3c004020,3d800040,3c008100,3c004020,3d800040,3c008020,3c020080
  //   ,13e010000,8*3c000000,3c004020,3d800040,3c008100,3c804020,3d000040
  //   ,13c008200,10*3c000000,3c004020,3d800040,3c008100,3c804020,3d000040
  //   ,13c008200,10*3c000000,3c004020,3d800040,3c008100,100020,3d000040
  //   ,13c008200,10*3c000000,3c004020,3d800040,3c008100,13c000000,12*3c000000
  //   ,3c004020,3d800040,3c008100,13c000000,12*3c000000,3c004020,3d800040
  //   ,3c008100,13c000000,12*3c000000,3c004020,3d800040,3c008100,13c000000
  //   ,12*3c000000,3c004020,3d800040,3c008100,13c000000,12*3c000000
  //   ,3c004020,3d800040,3c008100,13c000000,12*3c000000,3c004020,3d800040
  //   ,3c008100,13c000000,12*3c000000,3c004020,3d800040,3c008100,13c000000
  //   ,12*3c000000,3c004020,3d800040,3c008100,100100600,12*3c000000
  //   ,3c004020,3d800040,3c008100,104100600,12*3c000000,3c004020,3d800040
  //   ,3c008100,130100200,12*3c000000,3c004020,3d800040,3c008100,134100200
  //   ,12*3c000000,3c004020,3d800040,3c008100,108100600,12*3c000000
  //   ,3c004020,3d800040,3c008100,10c100600,12*3c000000,3c004020,3d800040
  //   ,3c008100,138100600,12*3c000000,3c004020,3d800040,3c008100,110100600
  //   ,12*3c000000,3c004020,3d800040,3c008100,114100600,12*3c000000
  //   ,3c004020,3d800040,3c008100,118100600,12*3c000000,3c004020,3d800040
  //   ,3c008100,11c100600,12*3c000000,3c004020,3d800040,3c008100,120100600
  //   ,12*3c000000,3c004020,3d800040,3c008100,124100600,12*3c000000
  //   ,3c004020,3d800040,3c008100,128100600,12*3c000000,3c004020,3d800040
  //   ,3c008100,12c100600,12*3c000000,3c004020,3d800040,3c008100,104000400
  //   ,12*3c000000,3c004020,3d800040,3c008100,3c004020,3d800040,13c008010
  //   ,10*3c000000,3c004020,3d800040,3c008100,80000000,3c004020,3d800040
  //   ,13c008010,9*3c000000,3c004020,3d800040,3c008100,13c020010,12*3c000000
  //   ,3c004020,3d800040,3c008100,80000000,13c020010,11*3c000000,3c004020
  //   ,3d800040,3c008100,3c804020,3d000040,3c002020,3c004080,3e010002
  //   ,13c008010,7*3c000000,3c004020,3d800040,3c008100,80000000,3c804020
  //   ,3d000040,3c002020,3c004080,3e010002,13c008010,6*3c000000,3c004020
  //   ,3d800040,3c008100,3c000001,3c002020,3d000040,13c008010,9*3c000000
  //   ,3c004020,3d800040,3c008100,3ca04020,3d000040,3c080080,43c000000
  //   ,3c002020,3e010002,3c002020,3c004080,3e010002,13c008010,3c000000,3c000000,3c000000
  //   ,3c004020,3d800040,3c008100,bc000000,3ca04020,3d000040,3c080080
  //   ,43c000000,3c002020,3e010002,3c002020,3c004080,3e010002,13c008010
  //   ,3c000000,3c000000,3c004020,3d800040,3c008100,93c000000,12*3c000000
  //   ,3c004020,3d800040,3c008100,93c000000,12*3c000000,3c004020,3d800040
  //   ,3c008100,93c000000,12*3c000000,3c004020,3d800040,3c008100,13c000000
  //   ,12*3c000000,3c004020,3d800040,3c008100,13c000000,12*3c000000
  //   ,3c004020,3d800040,3c008100,13c000000,12*3c000000,3c004020,3d800040
  //   ,3c008100,13c000000,12*3c000000,3c004020,3d800040,3c008100,3c002020
  //   ,3c020080,13e010002,10*3c000000,3c004020,3d800040,3c008100,3c000001
  //   ,3c002020,3d000040,13c008200,9*3c000000,3c004020,3d800040,3c008100
  //   ,13c020008,12*3c000000,3c004020,3d800040,3c008100,13c002200,12*3c000000
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  //   contents of CU_K (hex, n*v repeats v):
  //   3c004020,3d800040,3c008100,13c000000,12*3c000000,3c004020,3d800040
  //   ,3c008100,13c000000,12*3c000000,3c004020,3d800040,3c008100,13c000000
  //   ,12*3c000000,3c004020,3d800040,3c008100,13c000000,12*3c000000
  //   ,3c004020,3d800040,3c008100,13c000000,12*3c000000,3c004020,3d800040
  //   ,3c008100,13c000000,12*3c000000,3c004020,3d800040,3c008100,13c000000
  //   ,12*3c000000,3c004020,3d800040,3c008100,13c000000,12*3c000000
  //   ,3c004020,3d800040,3c008100,13c000000,12*3c000000,3c004020,3d800040
  //   ,3c008100,13c000000,12*3c000000,3c004020,3d800040,3c008100,13c000000
  //   ,12*3c000000,3c004020,3d800040,3c008100,13c000000,12*3c000000
  //   ,3c004020,3d800040,3c008100,13c000000,12*3c000000,3c004020,3d800040
  //   ,3c008100,13c000000,12*3c000000,3c004020,3d800040,3c008100,13c000000
  //   ,12*3c000000,3c004020,3d800040,3c008100,13c000000,12*3c000000
  //   ,3c004020,3d800040,3c008100,13c020200,12*3c000000,3c004020,3d800040
  //   ,3c008100,3c040020,3d000040,13c008200,10*3c000000,3c004020,3d800040
  //   ,3c008100,3c040020,3c020080,13e010000,10*3c000000,3c004020,3d800040
  //   ,3c008100,3c004020,3d800040,3c008020,3d000040,13c008200,8*3c000000
  //   ,3c004020,3d800040,3c008100,3c004020,3d800040,3c008020,3c020080
  //   ,13e010000,8*3c000000,3c004020,3d800040,3c008100,3c804020,3d000040
  //   ,13c008200,10*3c000000,3c004020,3d800040,3c008100,3c804020,3d000040
  //   ,13c008200,10*3c000000,3c004020,3d800040,3c008100,100020,3d000040
  //   ,13c008200,10*3c000000,3c004020,3d800040,3c008100,13c000000,12*3c000000
  //   ,3c004020,3d800040,3c008100,13c000000,12*3c000000,3c004020,3d800040
  //   ,3c008100,13c000000,12*3c000000,3c004020,3d800040,3c008100,13c000000
  //   ,12*3c000000,3c004020,3d800040,3c008100,13c000000,12*3c000000
  //   ,3c004020,3d800040,3c008100,13c000000,12*3c000000,3c004020,3d800040
  //   ,3c008100,13c000000,12*3c000000,3c004020,3d800040,3c008100,13c000000
  //   ,12*3c000000,3c004020,3d800040,3c008100,100100600,12*3c000000
  //   ,3c004020,3d800040,3c008100,104100600,12*3c000000,3c004020,3d800040
  //   ,3c008100,130100200,12*3c000000,3c004020,3d800040,3c008100,134100200
  //   ,12*3c000000,3c004020,3d800040,3c008100,108100600,12*3c000000
  //   ,3c004020,3d800040,3c008100,10c100600,12*3c000000,3c004020,3d800040
  //   ,3c008100,138100600,12*3c000000,3c004020,3d800040,3c008100,110100600
  //   ,12*3c000000,3c004020,3d800040,3c008100,114100600,12*3c000000
  //   ,3c004020,3d800040,3c008100,118100600,12*3c000000,3c004020,3d800040
  //   ,3c008100,11c100600,12*3c000000,3c004020,3d800040,3c008100,120100600
  //   ,12*3c000000,3c004020,3d800040,3c008100,124100600,12*3c000000
  //   ,3c004020,3d800040,3c008100,128100600,12*3c000000,3c004020,3d800040
  //   ,3c008100,12c100600,12*3c000000,3c004020,3d800040,3c008100,104000400
  //   ,12*3c000000,3c004020,3d800040,3c008100,3c004020,3d800040,13c008010
  //   ,10*3c000000,3c004020,3d800040,3c008100,80000000,3c004020,3d800040
  //   ,13c008010,9*3c000000,3c004020,3d800040,3c008100,13c020010,12*3c000000
  //   ,3c004020,3d800040,3c008100,80000000,13c020010,11*3c000000,3c004020
  //   ,3d800040,3c008100,3c804020,3d000040,3c002020,3c004080,3e010002
  //   ,13c008010,7*3c000000,3c004020,3d800040,3c008100,80000000,3c804020
  //   ,3d000040,3c002020,3c004080,3e010002,13c008010,6*3c000000,3c004020
  //   ,3d800040,3c008100,3c000001,3c002020,3d000040,13c008010,9*3c000000
  //   ,3c004020,3d800040,3c008100,3ca04020,3d000040,3c080080,43c000000
  //   ,3c002020,3e010002,3c002020,3c004080,3e010002,13c008010,3c000000,3c000000,3c000000
  //   ,3c004020,3d800040,3c008100,bc000000,3ca04020,3d000040,3c080080
  //   ,43c000000,3c002020,3e010002,3c002020,3c004080,3e010002,13c008010
  //   ,3c000000,3c000000,3c004020,3d800040,3c008100,3c400001,3c002020
  //   ,3d000040,3c008011,3c002020,3d000040,13c008800,6*3c000000,3c004020
  //   ,3d800040,3c008100,13c400000,12*3c000000,3c004020,3d800040,3c008100
  //   ,13c200000,12*3c000000,3c004020,3d800040,3c008100,13c000000,12*3c000000
  //   ,3c004020,3d800040,3c008100,13c000000,12*3c000000,3c004020,3d800040
  //   ,3c008100,13c000000,12*3c000000,3c004020,3d800040,3c008100,13c000000
  //   ,12*3c000000,3c004020,3d800040,3c008100,3c002020,3c020080,13e010002
  //   ,10*3c000000,3c004020,3d800040,3c008100,3c000001,3c002020,3d000040
  //   ,13c008200,9*3c000000,3c004020,3d800040,3c008100,13c020008,12*3c000000
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  //   ALU
  //   MPU
  //   GPU
  //   LDMA
  //   contents of ROM (hex, n*v repeats v):
  //   30,4,30,a55e,e15,2000000,e0042,e0048,3b,34,d,30,b2e,46,45,e43
  //   ,f15,b,efe20,e0042,e49,4e012,a49,f15,1,afa20,15,8000000,b11,15
  //   ,5000000,115,5b,10012,215,0,115,a,315,1,c15,9,a2d20,b1426,4d012
  //   ,23220,b1d25,bc02f,d0b10,300031,2a,b15,0,2b02f,200031,43,a3a21
  //   ,c15,30,a2d20,dd11,dcd20,d0012,23221,2b02f,500031,3b,215,20,20012
  //   ,315,6d,30012,315,73,30012,315,5d,30012,20012,315,49,30012,315
  //   ,6e,30012,a15,69,a0012,b15,74,b0012,a0012,b15,61,b0012,b15,6c
  //   ,b0012,a0012,b15,7a,b0012,a0012,30012,315,67,30012,20012,215,52
  //   ,20012,215,41,20012,215,4d,20012,215,2e,20012,10012,e49,e411,44
  //   ,47,36,46,45,e43,f15,8,efe20,e0042,e49,4e012,249,f15,2,2f220,2012
  //   ,49,f15,3,f020,10012,49,f15,4,f020,115,ff,10012,2111,11,10128
  //   ,12012,15,1ffe075,11,115,0,102f,200031,ca,30,a7,15,1ffe075,115
  //   ,0,10012,49,f15,2,f020,11,115,a,102f,500031,c8,30,b8,49,f15,1
  //   ,f020,115,0,10012,49,f15,5,f020,115,1,10012,30,18a,30,ca,15,1ffe080
  //   ,11,149,f15,6,1f120,1012,1011,215,f0,2024,215,1ffd7d5,2020,249
  //   ,f15,7,2f220,2012,1011,115,0,102f,200031,f6,30,e6,49,f15,7,f020
  //   ,11,115,13,1020,11,115,0,102f,500031,10d,30,f6,49,f15,2,f020,11
  //   ,34,194,49,f15,1,f020,115,0,10012,49,f15,5,f020,115,1,10012,30
  //   ,188,49,f15,7,f020,11,115,15,1020,11,115,0,102f,500031,134,30
  //   ,11d,49,f15,2,f020,11,34,194,49,f15,1,f020,115,0,10012,49,f15
  //   ,5,f020,115,1,10012,30,188,15,1ffe071,111,215,1,12120,215,ffff
  //   ,12128,10012,11,115,0,102f,500031,14d,30,146,15,1ffe071,115,1
  //   ,10012,30,14d,449,f15,6,4f420,4011,115,1ffe071,1111,215,1ffe072
  //   ,2211,12124,249,f15,2,2f220,2211,1212a,215,a5000000,1212a,34,1b0
  //   ,4011,115,1ffe085,1111,102f,500031,176,30,16d,49,f15,3,f020,11
  //   ,34,261,30,17a,15,0,30,17a,149,f15,1,1f120,1012,49,f15,5,f020
  //   ,115,1,10012,30,188,30,18a,49,f15,1,f020,11,e49,e411,44,47,36
  //   ,115,1ffdfef,1311,215,1,32320,a15,7f,3a328,a15,1ffdff0,aa11,3a02f
  //   ,500031,1a9,15,1ffe073,111,12120,10012,36,1211,a15,1ffdff1,2a220
  //   ,2012,31012,36,46,45,e43,f15,6,efe20,e0042,e49,4e012,249,f15,1
  //   ,2f220,2012,49,f15,2,f020,10012,2011,115,f0,1024,115,1ffd7d5,1020
  //   ,449,f15,3,4f420,4012,4011,115,5d,1020,11,34,a586,149,f15,4,1f120
  //   ,1012,1011,4111,215,5c,12120,1111,102f,500031,1fa,30,1e6,49,f15
  //   ,3,f020,11,115,5e,1020,111,215,1,12120,10012,49,f15,5,f020,20012
  //   ,30,25a,49,f15,2,f020,11,149,f15,3,1f120,1211,315,5d,23a20,aa11
  //   ,2a220,a15,1c,2a220,2012,49,f15,4,f020,11,1211,23220,2012,1011
  //   ,115,5f,1020,11,115,0,102f,200031,244,30,221,49,f15,3,f020,111
  //   ,215,5f,12120,215,0,21012,111,315,65,13120,21012,111,315,60,13120
  //   ,21012,111,315,63,13120,21012,11,115,62,1020,115,1,10012,30,251
  //   ,49,f15,3,f020,11,115,60,1020,115,1,10012,30,251,49,f15,5,f020
  //   ,115,0,10012,30,25a,30,25c,e49,e411,44,47,36,46,45,e43,f15,2,efe20
  //   ,e0042,149,f15,1,1f120,1012,15,1ffe085,11,115,0,102f,500031,27d
  //   ,30,277,49,115,0,10012,30,288,49,f15,1,f020,11,34,9d2,149,1012
  //   ,30,288,49,11,44,47,36,46,45,e43,f15,9,efe20,e0042,e49,4e012,249
  //   ,f15,2,2f220,2012,49,f15,3,f020,10012,15,1ffd676,111,315,1,13120
  //   ,10012,15,8000000,11,115,1ffd675,1012,15,1ffd674,30012,49,f15
  //   ,4,f020,115,ff,10012,2111,11,10128,12012,15,1ffe076,11,115,0,102f
  //   ,200031,2e8,30,2c5,15,1ffe076,115,0,10012,49,f15,2,f020,11,115
  //   ,a,102f,500031,2e6,30,2d6,49,f15,1,f020,115,0,10012,49,f15,5,f020
  //   ,115,1,10012,30,3be,30,2e8,15,1ffe081,11,149,f15,6,1f120,1012
  //   ,1011,215,f0,2024,215,1ffd7d5,2020,249,f15,7,2f220,2012,1011,115
  //   ,0,102f,200031,324,30,304,49,f15,7,f020,11,115,13,1020,11,115
  //   ,0,102f,200031,324,30,314,49,f15,7,f020,11,115,15,1020,11,115
  //   ,0,102f,500031,368,30,324,15,1ffd670,11,115,1,1020,115,7f,1028
  //   ,149,f15,8,1f120,1012,1011,115,1ffd677,1111,102f,200031,34f,30
  //   ,33b,49,f15,2,f020,11,115,1ffd670,1211,315,1ffd678,23220,2012
  //   ,49,f15,8,f020,11,1012,30,358,15,1ffd6f9,111,215,1,12120,10012
  //   ,30,358,49,f15,1,f020,115,0,10012,49,f15,5,f020,115,1,10012,30
  //   ,3bc,15,1ffd6f8,111,215,1,12120,215,ffff,12128,10012,11,115,0
  //   ,102f,500031,381,30,37a,15,1ffd6f8,115,1,10012,30,381,449,f15
  //   ,6,4f420,4011,115,1ffd6f8,1111,215,1ffe072,2211,12124,249,f15
  //   ,2,2f220,2211,1212a,215,a5000000,1212a,34,1b0,4011,115,1ffe085
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  //   contents of Storage (hex, n*v repeats v):
  //   41534653,2,10,2fb9b,1b,10,28,1000,3,7*0,1,1000,10ca,47aeef6b,63
  //   ,61,6c,63,75,6c,61,74,6f,72,23*0,10ca,0,0,1,20ca,b4a,f594a444
  //   ,67,75,65,73,73,2d,6e,75,6d,62,65,72,21*0,b4a,0,0,1,2c14,22c8
  //   ,8e786e5c,73,6e,61,6b,65,28*0,22c8,0,0,1,4edc,18b2,150d1315,6d
  //   ,61,7a,65,29*0,18b2,0,0,1,678e,1acf,8b7c5d4f,67,6f,6d,6f,6b,75
  //   ,27*0,1acf,0,0,1,825d,1f8f,c7044488,74,65,74,72,69,73,27*0,1f8f
  //   ,0,0,1,a1ec,1699,f384cc41,65,64,69,74,6f,72,27*0,1699,0,0,1,b885
  //   ,47e2,a0a52d31,63,6f,6d,70,69,6c,65,72,25*0,47e2,0,0,1,10067,34d
  //   ,72783483,70,72,6f,63,65,73,73,2d,64,65,6d,6f,21*0,34d,0,0,3,0,0,0
  //   ,64,6f,63,73,32*0,2,103b4,18d,8c39,77,65,6c,63,6f,6d,65,2e,74
  //   ,78,74,21*0,a,800,0,0,2,10bb4,8c,30d4,6e,6f,74,65,73,2e,74,78
  //   ,74,23*0,a,800,0,0,3,0,0,0,74,69,6e,79,63,31*0,2,113b4,94,246f
  //   ,68,65,6c,6c,6f,2e,63,25*0,d,800,0,0,2,11bb4,f3,3ec6,6b,65,79
  //   ,73,2e,63,26*0,d,800,0,0,2,123b4,175,7142,72,65,63,75,72,73,69
  //   ,6f,6e,2e,63,21*0,d,800,0,0,2,12bb4,2be,b288,61,72,72,61,79,73
  //   ,2e,63,24*0,d,800,0,0,2,133b4,1ec,868b,70,6f,69,6e,74,65,72,73
  //   ,2e,63,22*0,d,800,0,0,2,13bb4,6eb,26841,72,65,61,64,6d,65,2e,74
  //   ,78,74,22*0,d,800,0,0,2,143b4,75b7,224164,63,6f,6d,70,69,6c,65
  //   ,72,2e,63,22*0,d,10000,0,0,1,243b4,5505,ec320afd,63,6f,6d,70,69
  //   ,6c,65,72,32,24*0,5505,0,0,0,298b9,248,4e478f7f,61,72,72,61,79
  //   ,73,27*0,248,0,0,2,29b01,23,99a,74,65,73,74,2e,63,26*0,d,800,0,0,0
  //   ,2a301,ae,c60520fe,74,65,73,74,29*0,ae,0,0,0,2a3af,9f,4601f320
  //   ,74,65,73,74,32,28*0,9f,0,0,1,2a44e,5505,ec320afd,63,6f,6d,70
  //   ,69,6c,65,72,33,24*0,5505,0,0,0,2f953,248,4e478f7f,61,72,72,61
  //   ,79,73,32,26*0,248,3002*0,41455845,1,10,10ca,80000000,3,2,1,10
  //   ,6,1,5*0,80000000,16,10b4,10b4,1,0,30,80000009,15,7,37,2,0,30
  //   ,6,e15,82000000,e0042,e0048,e43,f15,24,efe20,e0042,e49,f15,5,efe20
  //   ,4e012,e49,f15,4,efe20,5e012,e49,f15,3,efe20,6e012,e49,f15,2,efe20
  //   ,7e012,e49,f15,1,efe20,8e012,e49,9e012,15,813fffd2,115,a,e49,f15
  //   ,f,efe20,1e012,10012,15,813fffd3,115,49,e49,f15,1a,efe20,1e012
  //   ,10012,15,813fffd4,715,6e,70012,15,813fffd5,115,70,e49,f15,6,efe20
  //   ,1e012,10012,15,813fffd6,c15,75,c0012,15,813fffd7,115,74,10012
  //   ,10d10,15,813fffd8,515,20,50012,15,813fffd9,815,65,80012,15,813fffda
  //   ,a15,76,a0012,a0310,e49,f15,14,efe20,3e012,15,813fffdb,80012,15
  //   ,813fffdc,70012,15,813fffdd,d0012,d0410,15,813fffde,50012,15,813fffdf
  //   ,a15,71,a0012,15,813fffe0,e49,f15,15,efe20,ce012,c0012,15,813fffe1
  //   ,80012,15,813fffe2,c0012,15,813fffe3,80012,15,813fffe4,50012,15
  //   ,813fffe5,215,6f,20012,e49,f15,e,efe20,2e012,15,813fffe6,30012
  //   ,15,813fffe7,80012,15,813fffe8,c15,72,c0012,15,813fffe9,a15,66
  //   ,a0012,15,813fffea,d15,6c,d0012,d0910,e49,f15,1e,efe20,9e012,15
  //   ,813fffeb,20012,15,813fffec,d15,77,e49,f15,13,efe20,de012,d0012
  //   ,15,813fffed,315,2e,30012,15,813fffee,50012,15,813fffef,115,45
  //   ,e49,f15,7,efe20,1e012,10012,15,813ffff0,115,78,e49,f15,b,efe20
  //   ,1e012,10012,15,813ffff1,615,69,60012,15,813ffff2,40012,40210
  //   ,e49,f15,11,efe20,2e012,15,813ffff3,60012,15,813ffff4,70012,15
  //   ,813ffff5,b15,67,b0012,e49,f15,1f,efe20,be012,15,813ffff6,50012
  //   ,15,813ffff7,115,73,e49,f15,18,efe20,1e012,10012,d15,813ffff8
  //   ,415,61,4d012,d15,813ffff9,ad012,a15,813ffffa,8a012,a15,813ffffb
  //   ,9a012,a15,813ffffc,15,79,e49,f15,d,efe20,e012,a012,a15,813ffffd
  //   ,e49,f15,8,efe20,3e012,3a012,a15,813ffffe,e49,f15,f,ef117,1a012
  //   ,d15,813fffff,a15,0,ad012,d15,813fffcb,1d012,d15,813fffcc,915
  //   ,51,9d012,d15,813fffcd,e49,f15,15,ef017,d012,d15,813fffce,6d012
  //   ,d15,813fffcf,2d012,d15,813fffd0,3d012,d15,813fffd1,ad012,d15
  //   ,813fffa3,1d012,d15,813fffa4,915,57,9d012,d15,813fffa5,4d012,e49
  //   ,f15,c,efe20,4e012,d15,813fffa6,cd012,d15,813fffa7,7d012,d15,813fffa8
  //   ,6d012,e49,f15,19,efe20,6e012,d15,813fffa9,7d012,d15,813fffaa
  //   ,bd012,d15,813fffab,15,3a,e49,f15,9,efe20,e012,d012,d15,813fffac
  //   ,5d012,d15,813fffad,915,54,9d012,d15,813fffae,15,68,d012,e49,f15
  //   ,17,efe20,e012,d15,813fffaf,8d012,d15,813fffb0,cd012,d15,813fffb1
  //   ,8d012,d15,813fffb2,215,27,e49,f15,1c,efe20,2e012,2d012,d15,813fffb3
  //   ,cd012,d15,813fffb4,8d012,d15,813fffb5,5d012,d15,813fffb6,7d012
  //   ,d15,813fffb7,e49,f15,e,ef317,3d012,d15,813fffb8,5d012,d15,813fffb9
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endmodule
